// Logisim project FourBitParity.circ as structural Verilog: 4 circuits, main circuit implementation
module implementation (
  input  EnableIn,
  input  InputBitIn,
  input  ClkIn,
  output out_4
);

  wire [2:0] curr_state, next_state_logic_1_next_out;

  next_state_logic next_state_logic_1 (
    .bit_in(InputBitIn), .curr_in(curr_state), .next_out(next_state_logic_1_next_out));
  state state_1 (
    .state_in(next_state_logic_1_next_out), .enable_in(EnableIn), .clock_in(ClkIn), .stored_state(curr_state));
  output_logic output_logic_1 (.state_in(curr_state), .logic_out(out_4));

  // Other names for the same wires on the sheet: Clk = ClkIn; Enable = EnableIn; InputBit = InputBitIn;
  //   IsEvenOut = out_4
endmodule

module next_state_logic (
  input  bit_in,
  input  [2:0] curr_in,
  output [2:0] next_out
);

  wire and_1_out, and_2_out, and_3_out, and_4_out, and_5_out, and_6_out, and_7_out, and_8_out, and_9_out,
       not_1_out, not_2_out, not_4_out;

  not not_1 (not_1_out, bit_in);
  not not_2 (not_2_out, curr_in[2]);
  not not_3 (next_out[1], curr_in[1]);
  not not_4 (not_4_out, curr_in[0]);
  and and_1 (and_1_out, not_2_out, curr_in[1]);
  and and_2 (and_2_out, curr_in[2], next_out[1]);
  and and_3 (and_3_out, not_1_out, not_2_out, curr_in[1], curr_in[0]);
  and and_4 (and_4_out, not_1_out, curr_in[2], next_out[1], curr_in[0]);
  and and_5 (and_5_out, not_1_out, curr_in[2], curr_in[1], not_4_out);
  and and_6 (and_6_out, bit_in, not_2_out, next_out[1]);
  and and_7 (and_7_out, bit_in, not_2_out, not_4_out);
  and and_8 (and_8_out, bit_in, next_out[1], not_4_out);
  and and_9 (and_9_out, bit_in, curr_in[2], curr_in[1], curr_in[0]);
  or or_1 (next_out[2], and_1_out, and_2_out);
  or or_2 (next_out[0], and_3_out, and_4_out, and_5_out, and_6_out, and_7_out, and_8_out, and_9_out);
endmodule

module state (
  input  [2:0] state_in,
  input  enable_in,
  input  clock_in,
  output [2:0] stored_state
);

  Register #(.width(3)) register_1 (.D(state_in), .en(enable_in), .clk(clock_in), .Q(stored_state));  // open: clr
endmodule

module output_logic (
  input  [2:0] state_in,
  output logic_out
);

  wire not_1_out, not_2_out;

  not not_1 (not_1_out, state_in[2]);
  not not_2 (not_2_out, state_in[1]);
  and and_1 (logic_out, not_1_out, not_2_out, state_in[0]);
endmodule
