// Logisim project UpDownCounter.circ as structural Verilog: 3 circuits, main circuit implementation
module implementation (
  input  EnableIn,
  input  CountUpIn,
  input  CountDownIn,
  input  clkIn,
  output [2:0] Count
);

  wire [2:0] next_state_logic_1_next_state;

  next_state_logic next_state_logic_1 (
    .upIn(CountUpIn), .downIn(CountDownIn), .curr_state(Count), .next_state(next_state_logic_1_next_state));
  state state_1 (
    .next_state_in(next_state_logic_1_next_state), .enable_in(EnableIn), .clock_in(clkIn), .state_out(Count));

  // Other names for the same wires on the sheet: clk = clkIn; CountDown = CountDownIn; CountUp = CountUpIn;
  //   curr_state[2:0] = Count; Enable = EnableIn
endmodule

module next_state_logic (
  input  upIn,
  input  downIn,
  input  [2:0] curr_state,
  output [2:0] next_state
);

  wire and_1_out, and_2_out, and_3_out, and_4_out, and_5_out, and_6_out, and_7_out, and_8_out, and_9_out,
       and_10_out, and_11_out, and_12_out, and_13_out, and_14_out, and_15_out, and_16_out, and_17_out,
       not_1_out, not_2_out, not_3_out, not_4_out;

  not not_1 (not_1_out, upIn);
  not not_2 (not_2_out, downIn);
  not not_3 (not_3_out, curr_state[1]);
  not not_4 (not_4_out, curr_state[0]);
  and and_1 (and_1_out, not_2_out, curr_state[2]);
  and and_2 (and_2_out, curr_state[2], curr_state[0]);
  and and_3 (and_3_out, curr_state[2], curr_state[1]);
  and and_4 (and_4_out, upIn, not_2_out, curr_state[1], curr_state[0]);
  and and_5 (and_5_out, upIn, curr_state[2]);
  and and_6 (and_6_out, not_2_out, curr_state[1], not_4_out);
  and and_7 (and_7_out, not_1_out, curr_state[1], curr_state[0]);
  and and_8 (and_8_out, not_2_out, curr_state[2], curr_state[1]);
  and and_9 (and_9_out, not_1_out, downIn, curr_state[2], not_3_out, not_4_out);
  and and_10 (and_10_out, upIn, not_2_out, not_3_out, curr_state[0]);
  and and_11 (and_11_out, upIn, downIn, curr_state[1]);
  and and_12 (and_12_out, not_1_out, not_2_out, curr_state[0]);
  and and_13 (and_13_out, not_2_out, curr_state[2], curr_state[1], curr_state[0]);
  and and_14 (and_14_out, not_1_out, downIn, curr_state[1], not_4_out);
  and and_15 (and_15_out, not_1_out, downIn, curr_state[2], not_4_out);
  and and_16 (and_16_out, upIn, not_2_out, not_4_out);
  and and_17 (and_17_out, upIn, downIn, curr_state[0]);
  or or_1 (next_state[2], and_1_out, and_2_out, and_3_out, and_4_out, and_5_out);
  or or_2 (next_state[1], and_6_out, and_7_out, and_8_out, and_9_out, and_10_out, and_11_out);
  or or_3 (next_state[0], and_12_out, and_13_out, and_14_out, and_15_out, and_16_out, and_17_out);
endmodule

module state (
  input  [2:0] next_state_in,
  input  enable_in,
  input  clock_in,
  output [2:0] state_out
);

  Register #(.width(3)) register_1 (.D(next_state_in), .en(enable_in), .clk(clock_in), .Q(state_out));  // open: clr
endmodule
