// Logisim project Vending.circ as structural Verilog: 4 circuits, main circuit implementation
module implementation (
  input  EnableIn,
  input  QuarterReceivedIn,
  input  DimeReceivedIn,
  input  NickelReceivedIn,
  input  ClkIn,
  output Give_Mechandise_Out,
  output Give_Dime_Out,
  output Give_Nickel_Out
);

  wire [2:0] input_logic_1_next_out, state_1_stored_state;

  input_logic input_logic_1 (
    .n_in(NickelReceivedIn), .d_in(DimeReceivedIn), .q_in(QuarterReceivedIn),
    .state_in(state_1_stored_state), .next_out(input_logic_1_next_out));
  state state_1 (
    .state_in(input_logic_1_next_out), .enable_in(EnableIn), .clock_in(ClkIn),
    .stored_state(state_1_stored_state));
  output_logic output_logic_1 (
    .n_in(NickelReceivedIn), .d_in(DimeReceivedIn), .q_in(QuarterReceivedIn),
    .state_in(state_1_stored_state), .g_m_out(Give_Mechandise_Out), .g_d_out(Give_Dime_Out),
    .g_n_out(Give_Nickel_Out));

  // Other names for the same wires on the sheet: clk = ClkIn; DimeReceieved = DimeReceivedIn; Enable = EnableIn;
  //   Give_Dime = Give_Dime_Out; Give_Merchandise = Give_Mechandise_Out; Give_Nickel = Give_Nickel_Out;
  //   NickelReceieved = NickelReceivedIn; QuarterReceieved = QuarterReceivedIn
endmodule

module input_logic (
  input  n_in,
  input  d_in,
  input  q_in,
  input  [2:0] state_in,
  output [2:0] next_out
);

  wire and_1_out, and_2_out, and_3_out, and_4_out, and_5_out, and_6_out, and_7_out, and_8_out, and_9_out,
       and_10_out, and_11_out, and_12_out, and_13_out, and_14_out, not_1_out, not_2_out, not_3_out,
       not_4_out, not_5_out, not_6_out;

  not not_1 (not_1_out, n_in);
  not not_2 (not_2_out, d_in);
  not not_3 (not_3_out, q_in);
  not not_4 (not_4_out, state_in[2]);
  not not_5 (not_5_out, state_in[1]);
  not not_6 (not_6_out, state_in[0]);
  and and_1 (and_1_out, not_1_out, not_2_out, not_3_out, state_in[2]);
  and and_2 (and_2_out, not_1_out, not_3_out, state_in[2], not_5_out);
  and and_3 (and_3_out, n_in, not_2_out, not_3_out, not_4_out, not_6_out);
  and and_4 (and_4_out, not_1_out, not_2_out, not_3_out, state_in[1]);
  and and_5 (and_5_out, not_2_out, not_3_out, state_in[1], not_6_out);
  and and_6 (and_6_out, not_1_out, d_in, not_3_out, not_4_out, not_6_out);
  and and_7 (and_7_out, not_1_out, d_in, not_3_out, state_in[2], not_5_out);
  and and_8 (and_8_out, n_in, not_2_out, not_3_out, state_in[2], not_5_out);
  and and_9 (and_9_out, not_1_out, not_2_out, not_3_out, state_in[0]);
  and and_10 (and_10_out, not_2_out, not_3_out, state_in[1], state_in[0]);
  and and_11 (and_11_out, not_1_out, not_2_out, q_in, not_4_out, not_5_out, not_6_out);
  and and_12 (and_12_out, not_1_out, d_in, not_3_out, state_in[1], not_6_out);
  and and_13 (and_13_out, not_1_out, d_in, not_3_out, state_in[2], state_in[1]);
  and and_14 (and_14_out, n_in, not_2_out, not_3_out, state_in[2], state_in[1]);
  or or_1 (next_out[2], and_1_out, and_2_out, and_3_out);
  or or_2 (next_out[1], and_4_out, and_5_out, and_6_out, and_7_out, and_8_out);
  or or_3 (next_out[0], and_9_out, and_10_out, and_11_out, and_12_out, and_13_out, and_14_out);
endmodule

module output_logic (
  input  n_in,
  input  d_in,
  input  q_in,
  input  [2:0] state_in,
  output g_m_out,
  output g_d_out,
  output g_n_out
);

  wire and_1_out, and_2_out, and_3_out, and_4_out, and_5_out, and_6_out, and_7_out, and_8_out, and_9_out,
       and_10_out, not_1_out, not_2_out, not_3_out, not_4_out, not_5_out;

  not not_1 (not_1_out, n_in);
  not not_2 (not_2_out, d_in);
  not not_3 (not_3_out, q_in);
  not not_4 (not_4_out, state_in[2]);
  not not_5 (not_5_out, state_in[1]);
  and and_1 (and_1_out, not_1_out, not_2_out, q_in, state_in[0]);
  and and_2 (and_2_out, not_1_out, not_2_out, q_in, state_in[1]);
  and and_3 (and_3_out, not_1_out, not_2_out, q_in, state_in[2]);
  and and_4 (and_4_out, not_1_out, d_in, not_3_out, state_in[0]);
  and and_5 (and_5_out, n_in, not_2_out, not_3_out, not_5_out, state_in[0]);
  and and_6 (and_6_out, not_1_out, not_2_out, q_in, state_in[0]);
  and and_7 (and_7_out, not_1_out, not_2_out, q_in, state_in[2], state_in[1]);
  and and_8 (and_8_out, not_1_out, not_2_out, q_in, state_in[0]);
  and and_9 (and_9_out, not_1_out, not_2_out, q_in, not_4_out, state_in[1]);
  and and_10 (and_10_out, not_1_out, d_in, not_3_out, not_5_out, state_in[0]);
  or or_1 (g_m_out, and_1_out, and_2_out, and_3_out, and_4_out, and_5_out);
  or or_2 (g_d_out, and_6_out, and_7_out);
  or or_3 (g_n_out, and_8_out, and_9_out, and_10_out);
endmodule

module state (
  input  [2:0] state_in,
  input  enable_in,
  input  clock_in,
  output [2:0] stored_state
);

  Register #(.width(3)) register_1 (.D(state_in), .en(enable_in), .clk(clock_in), .Q(stored_state));  // open: clr
endmodule
